// Logisim project Circuito2.circ as structural Verilog: 1 circuit, main circuit main
module main (
  input  M
);

  wire and_1_out, and_2_out, and_3_out, and_4_out, clock_1_out, F0_qn, F1_qn, not_1_out, not_2_out, or_1_out,
       or_2_out;
  wire [2:0] F0_q;

  Clock clock_1 (.out(clock_1_out));
  J_K_Flip_Flop F0 (.J(1'b1), .K(1'b1), .clk(clock_1_out), .Q(F0_q[0]), .Qn(F0_qn));  // open: preset, reset
  not not_1 (not_1_out, M);
  and and_1 (and_1_out, F0_q[0], M);
  and and_2 (and_2_out, F0_qn, not_1_out);
  or or_1 (or_1_out, and_1_out, and_2_out);
  J_K_Flip_Flop F1 (.J(1'b1), .K(1'b1), .clk(or_1_out), .Q(F0_q[1]), .Qn(F1_qn));  // open: preset, reset
  and and_3 (and_3_out, F0_q[1], M);
  not not_2 (not_2_out, M);
  and and_4 (and_4_out, F1_qn, not_2_out);
  or or_2 (or_2_out, and_3_out, and_4_out);
  J_K_Flip_Flop F2 (.J(1'b1), .K(1'b1), .clk(or_2_out), .Q(F0_q[2]));  // open: Qn, preset, reset
  Hex_Digit_Display hex_digit_display_1 (.value({1'b0, F0_q}));  // open: dp
endmodule
