// Logisim project Circuito3.circ as structural Verilog: 1 circuit, main circuit main
module main (
  input  X,
  output Y
);

  wire A_q, A_qn, and_1_out, and_2_out, B_q, clock_1_out, not_1_out, or_1_out;

  Clock clock_1 (.out(clock_1_out));
  D_Flip_Flop A (.D(and_2_out), .clk(clock_1_out), .Q(A_q), .Qn(A_qn));  // open: preset, reset
  D_Flip_Flop B (.D(and_1_out), .clk(clock_1_out), .Q(B_q));  // open: Qn, preset, reset
  not not_1 (not_1_out, X);
  or or_1 (or_1_out, A_q, B_q);
  and and_1 (and_1_out, A_qn, X);
  and and_2 (and_2_out, or_1_out, X);
  and and_3 (Y, or_1_out, not_1_out);
endmodule
