// Logisim project IOC_TRABALHO_PRATICO_3.circ as structural Verilog
module carro4 (
  input  A,
  output Q0,
  output Q1,
  output Q2,
  output r
);

  wire and_1_out, and_2_out, and_3_out, and_4_out, and_5_out, clock_1_out, not_1_out, not_2_out, not_3_out,
       not_4_out, not_5_out, not_6_out, or_1_out, or_2_out;

  not not_1 (not_1_out, Q2);
  not not_2 (not_2_out, Q0);
  and and_1 (and_1_out, not_1_out, not_2_out, A);
  Clock clock_1 (.out(clock_1_out));
  and and_2 (and_2_out, Q1, not_3_out);
  or or_1 (or_1_out, and_1_out, and_2_out);
  D_Flip_Flop d_ff_1 (.D(or_1_out), .clk(clock_1_out), .Q(Q0));  // open: Qn, preset, reset
  not not_3 (not_3_out, Q0);
  not not_4 (not_4_out, Q1);
  and and_3 (and_3_out, Q0, not_4_out);
  or or_2 (or_2_out, and_3_out, and_4_out);
  D_Flip_Flop d_ff_2 (.D(or_2_out), .clk(clock_1_out), .Q(Q1));  // open: Qn, preset, reset
  not not_5 (not_5_out, Q0);
  and and_4 (and_4_out, Q1, not_5_out);
  not not_6 (not_6_out, Q2);
  and and_5 (and_5_out, Q0, not_6_out, Q1);
  D_Flip_Flop d_ff_3 (.D(and_5_out), .clk(clock_1_out), .Q(Q2));  // open: Qn, preset, reset
  or or_3 (r, Q2, Q0);
endmodule

module maquinaDeVendas5 (
  input  A,
  input  B,
  output out_3
);

  wire clock_1_out, d_ff_1_q, d_ff_2_q, d_ff_3_q, logicacombinacional5_1_d0, logicacombinacional5_1_d1,
       logicacombinacional5_1_d2;

  Clock clock_1 (.out(clock_1_out));
  D_Flip_Flop d_ff_1 (.D(logicacombinacional5_1_d0), .clk(clock_1_out), .Q(d_ff_1_q));  // open: Qn, preset, reset
  D_Flip_Flop d_ff_2 (.D(logicacombinacional5_1_d1), .clk(clock_1_out), .Q(d_ff_2_q));  // open: Qn, preset, reset
  D_Flip_Flop d_ff_3 (.D(logicacombinacional5_1_d2), .clk(clock_1_out), .Q(d_ff_3_q));  // open: Qn, preset, reset
  logicaCombinacional5 logicacombinacional5_1 (
    .Q2(d_ff_3_q), .Q1(d_ff_2_q), .Q0(d_ff_1_q), .A(A), .B(B), .D2(logicacombinacional5_1_d2),
    .D1(logicacombinacional5_1_d1), .D0(logicacombinacional5_1_d0), .P(out_3));
endmodule

module logicaCombinacional5 (
  input  Q2,
  input  Q1,
  input  Q0,
  input  A,
  input  B,
  output D2,
  output D1,
  output D0,
  output P
);

  wire and_1_out, and_2_out, and_3_out, and_4_out, and_5_out, and_6_out, and_7_out, and_8_out, and_9_out,
       and_10_out, and_11_out, and_12_out, and_13_out, not_1_out, not_2_out, not_3_out, not_4_out, not_5_out;

  not not_1 (not_1_out, Q2);
  not not_2 (not_2_out, Q1);
  not not_3 (not_3_out, Q0);
  not not_4 (not_4_out, A);
  not not_5 (not_5_out, B);
  and and_1 (and_1_out, not_1_out, Q1, B);
  and and_2 (and_2_out, not_1_out, A);
  and and_3 (and_3_out, Q1, Q0);
  and and_4 (and_4_out, Q2, not_2_out);
  and and_5 (and_5_out, not_2_out, B);
  and and_6 (and_6_out, Q2, not_2_out, A);
  and and_7 (and_7_out, not_2_out, Q0, not_4_out);
  and and_8 (and_8_out, not_1_out, Q1, not_3_out, not_5_out);
  and and_9 (and_9_out, not_1_out, Q1, A);
  and and_10 (and_10_out, not_2_out, not_3_out, not_4_out, not_5_out);
  and and_11 (and_11_out, not_1_out, Q0, B);
  and and_12 (and_12_out, not_1_out, not_2_out, Q0, A);
  and and_13 (and_13_out, not_1_out, not_3_out, not_4_out, not_5_out);
  and and_14 (P, Q2, Q1);
  or or_1 (D2, and_1_out, and_2_out, and_3_out, and_4_out);
  or or_2 (D1, and_5_out, and_6_out, and_7_out, and_8_out, and_9_out);
  or or_3 (D0, and_10_out, and_11_out, and_12_out, and_13_out);
endmodule

module circuito1 (
  input  in_1,
  input  clock,
  output Q0,
  output Q1,
  output Q2,
  output Q3
);

  wire nand_1_out, not_1_out, not_2_out, not_3_out, not_4_out;

  J_K_Flip_Flop #(.trigger("falling")) j_k_ff_1 (
    .J(in_1), .K(in_1), .clk(clock), .Q(Q0), .reset(not_1_out));  // open: Qn, preset
  not not_1 (not_1_out, nand_1_out);
  J_K_Flip_Flop #(.trigger("falling")) j_k_ff_2 (
    .J(in_1), .K(in_1), .clk(Q0), .Q(Q1), .reset(not_2_out));  // open: Qn, preset
  not not_2 (not_2_out, nand_1_out);
  J_K_Flip_Flop #(.trigger("falling")) j_k_ff_3 (
    .J(in_1), .K(in_1), .clk(Q1), .Q(Q2), .reset(not_3_out));  // open: Qn, preset
  not not_3 (not_3_out, nand_1_out);
  J_K_Flip_Flop #(.trigger("falling")) j_k_ff_4 (
    .J(in_1), .K(in_1), .clk(Q2), .Q(Q3), .reset(not_4_out));  // open: Qn, preset
  not not_4 (not_4_out, nand_1_out);
  nand nand_1 (nand_1_out, Q3, Q1);
endmodule
